// Logisim project Domaci_2.circ as structural Verilog: 1 circuit, main circuit main
module main (
  input  X1,
  input  X2,
  input  X3,
  input  X4,
  input  X5,
  output Y
);

  wire not_1_out;

  not not_1 (not_1_out, X3);
  nor nor_1 (Y, X1, X2, not_1_out, X4, X5);

  // Notes on the sheet:
  //   20.02.        2+2=4
endmodule
