// Logisim project Domaci_2_ORT.circ as structural Verilog: 1 circuit, main circuit Zadatak
module Zadatak (
  input  X1,
  input  X2,
  input  X3,
  input  X4,
  input  X5,
  output Y
);

  wire nor_1_out, nor_2_out, nor_3_out, nor_4_out, nor_5_out, nor_6_out, nor_7_out, nor_8_out, nor_9_out,
       nor_10_out, nor_11_out;

  nor nor_1 (nor_1_out, X1, X1);
  nor nor_2 (nor_2_out, X3, X3);
  nor nor_3 (nor_3_out, X4, X5);
  nor nor_4 (nor_4_out, nor_1_out, X2);
  nor nor_5 (nor_5_out, X2, nor_2_out);
  nor nor_6 (nor_6_out, nor_3_out, nor_3_out);
  nor nor_7 (nor_7_out, nor_4_out, nor_4_out);
  nor nor_8 (nor_8_out, nor_5_out, nor_5_out);
  nor nor_9 (nor_9_out, nor_8_out, nor_6_out);
  nor nor_10 (nor_10_out, nor_7_out, nor_2_out);
  nor nor_11 (nor_11_out, nor_9_out, nor_9_out);
  nor nor_12 (Y, nor_10_out, nor_11_out);

  // Notes on the sheet:
  //   Datum rodjenja 20.02. 
  //   zbir cifara je 4 - 00100 
endmodule
