// Logisim project vezbe_ort_9.circ as structural Verilog: 1 circuit, main circuit logickoKolo22
module logickoKolo22 (
  input  x1,
  input  x2,
  input  x3,
  input  x4,
  output f
);

  wire nand_1_out, nand_2_out, nand_3_out, nand_4_out;

  nand nand_1 (nand_1_out, x1, x1);
  nand nand_2 (nand_2_out, x4, x4);
  nand nand_3 (nand_3_out, nand_1_out, x3, nand_2_out);
  nand nand_4 (nand_4_out, x1, x2, x4);
  nand nand_5 (f, nand_3_out, nand_4_out);
endmodule
